// Logisim project 4TO1MUX.circ as structural Verilog
module _4TO1MUX (
  input  in_1,
  input  in_2,
  input  in_3,
  input  in_4,
  input  in_5,
  input  in_6,
  output out_7
);

  wire and_1_out, and_2_out, and_3_out, and_4_out, not_1_out, not_2_out;

  not not_1 (not_1_out, in_2);
  not not_2 (not_2_out, in_5);
  and and_1 (and_1_out, not_1_out, not_2_out, in_1);
  and and_2 (and_2_out, in_2, not_2_out, in_3);
  and and_3 (and_3_out, not_1_out, in_5, in_4);
  and and_4 (and_4_out, in_2, in_5, in_6);
  or or_1 (out_7, and_1_out, and_2_out, and_3_out, and_4_out);
endmodule
