// Logisim project rotr.circ as structural Verilog: 5 circuits, main circuit main
module main (
  input  [3:0] B,
  input  [15:0] A,
  output [15:0] Output
);

  wire [15:0] replace1_1_out_3, replace2_1_out_3, replace4_1_out_3;

  replace1 replace1_1 (.in_2(A), .in_1(B[0]), .out_3(replace1_1_out_3));
  replace2 replace2_1 (.in_2(replace1_1_out_3), .in_1(B[1]), .out_3(replace2_1_out_3));
  replace4 replace4_1 (.in_2(replace2_1_out_3), .in_1(B[2]), .out_3(replace4_1_out_3));
  replace8 replace8_1 (.in_2(replace4_1_out_3), .in_1(B[3]), .out_3(Output));

  // Other names for the same wires on the sheet: _0 = B[0]; _1 = B[1]; _2 = B[2]; _3 = B[3]
endmodule

module replace1 (
  input  in_1,
  input  [15:0] in_2,
  output [15:0] out_3
);

  Multiplexer #(.width(16), .enable("false")) multiplexer_1 (
    .in0(in_2), .in1({in_2[0], in_2[15:1]}), .out(out_3), .sel(in_1));
endmodule

module replace2 (
  input  in_1,
  input  [15:0] in_2,
  output [15:0] out_3
);

  Multiplexer #(.width(16), .enable("false")) multiplexer_1 (
    .in0(in_2), .in1({in_2[1:0], in_2[15:2]}), .out(out_3), .sel(in_1));
endmodule

module replace4 (
  input  in_1,
  input  [15:0] in_2,
  output [15:0] out_3
);

  Multiplexer #(.width(16), .enable("false")) multiplexer_1 (
    .in0(in_2), .in1({in_2[3:0], in_2[15:4]}), .out(out_3), .sel(in_1));
endmodule

module replace8 (
  input  in_1,
  input  [15:0] in_2,
  output [15:0] out_3
);

  Multiplexer #(.width(16), .enable("false")) multiplexer_1 (
    .in0(in_2), .in1({in_2[7:0], in_2[15:8]}), .out(out_3), .sel(in_1));
endmodule
