// Logisim project splitter.circ as structural Verilog
module Ex1 (
  input  [7:0] Input,
  output Out1,
  output [7:0] Out2
);

  not not_1 (Out2[7], Input[7]);
  and and_1 (Out1, Input[0], Input[7]);

  assign Out2[6:0] = Input[6:0];
endmodule
