// Logisim project Regfile.circ as structural Verilog: 1 circuit, main circuit main
module main (
  input  [1:0] Read_register_1,
  input  [1:0] Read_register_2,
  input  [1:0] write_register,
  input  [15:0] write_data,
  input  RegWrite,
  input  clock,
  output [15:0] Reg_0_Value,
  output [15:0] Reg_1_Value,
  output [15:0] Reg_2_Value,
  output [15:0] Reg_3_Value,
  output [15:0] Read_Data_1,
  output [15:0] Read_Data_2
);

  wire and_1_out, and_2_out, and_3_out, and_4_out, decoder_1_out0, decoder_1_out1, decoder_1_out2,
       decoder_1_out3;
  wire [15:0] demultiplexer_1_out0, demultiplexer_1_out1, demultiplexer_1_out2, demultiplexer_1_out3;

  Decoder #(.select(2), .enable("false")) decoder_1 (
    .out0(decoder_1_out0), .out1(decoder_1_out1), .out2(decoder_1_out2), .out3(decoder_1_out3),
    .sel(write_register));
  and and_1 (and_1_out, decoder_1_out0, RegWrite);
  and and_2 (and_2_out, decoder_1_out1, RegWrite);
  and and_3 (and_3_out, RegWrite, decoder_1_out2);
  and and_4 (and_4_out, RegWrite, decoder_1_out3);
  Demultiplexer #(.select(2), .width(16), .enable("false")) demultiplexer_1 (
    .out0(demultiplexer_1_out0), .out1(demultiplexer_1_out1), .out2(demultiplexer_1_out2),
    .out3(demultiplexer_1_out3), .in(write_data), .sel(write_register));
  Register #(.width(16)) register_1 (
    .D(demultiplexer_1_out0), .en(and_1_out), .Q(Reg_0_Value), .clk(clock));  // open: clr
  Register #(.width(16)) register_2 (
    .D(demultiplexer_1_out1), .en(and_2_out), .Q(Reg_1_Value), .clk(clock));  // open: clr
  Register #(.width(16)) register_3 (
    .D(demultiplexer_1_out2), .en(and_3_out), .Q(Reg_2_Value), .clk(clock));  // open: clr
  Register #(.width(16)) register_4 (
    .D(demultiplexer_1_out3), .en(and_4_out), .Q(Reg_3_Value), .clk(clock));  // open: clr
  Multiplexer #(.select(2), .width(16), .enable("false")) multiplexer_1 (
    .in0(Reg_0_Value), .in1(Reg_1_Value), .in2(Reg_2_Value), .in3(Reg_3_Value), .out(Read_Data_1),
    .sel(Read_register_1));
  Multiplexer #(.select(2), .width(16), .enable("false")) multiplexer_2 (
    .in0(Reg_0_Value), .in1(Reg_1_Value), .in2(Reg_2_Value), .in3(Reg_3_Value), .out(Read_Data_2),
    .sel(Read_register_2));

  // Other names for the same wires on the sheet: clk = clock; R0[15:0] = Reg_0_Value; R1[15:0] = Reg_1_Value;
  //   R2[15:0] = Reg_2_Value; R3[15:0] = Reg_3_Value; RegW = RegWrite; RR1[1:0] = Read_register_1;
  //   RR2[1:0] = Read_register_2; WData[15:0] = write_data; WR[1:0] = write_register

  // Notes on the sheet:
  //   These are INPUTS to the circuit
  //   These are INPUTS to the circuit
  //   DO NOT CHANGE THE LOCATIONS OF THE INPUTS/OUTPUTS! IF YOU DO SO, YOU NEED TO MAKE SURE THE PINS ARE AT THE RIGHT PLACE!
  //   Yet again, the clock is not an actual clock, but an input, one that will be driven from a higher circuit
  //   These are OUTPUTS to the circuit
  //   These are OUTPUTS to the circuit
endmodule
