// Logisim project alu.circ as structural Verilog: 11 circuits, main circuit main
module main (
  input  [15:0] X,
  input  [15:0] Y,
  input  [3:0] switch__S,
  output signed_overflow,
  output [15:0] result,
  output equal
);

  wire OF_ADD, OF_ADDP8, undriven;
  wire [15:0] add_1_out, addp8_1_out, and_1_out, or_1_out, sllv_1_out, slt_1_out, srav_1_out, srlv_1_out,
       sub_1_out, subp8_1_out;

  ADD add_1 (.X(X), .Y(Y), .out(add_1_out), .OverFlow(OF_ADD));
  SUB sub_1 (.X(X), .Y(Y), .out(sub_1_out), .OverFlow(OF_ADD));
  SLLV sllv_1 (.X(X), .Y(Y), .out(sllv_1_out));
  SRLV srlv_1 (.X(X), .Y(Y), .out(srlv_1_out));
  SRAV srav_1 (.X(X), .Y(Y), .out(srav_1_out));
  SLT slt_1 (.X(X), .Y(Y), .out(slt_1_out));
  OR or_1 (.X(X), .Y(Y), .out(or_1_out));
  AND and_1 (.X(X), .Y(Y), .out(and_1_out));
  ADDP8 addp8_1 (.X(X), .Y(Y), .out(addp8_1_out), .OverFlow(OF_ADDP8));
  SUBP8 subp8_1 (.X(X), .Y(Y), .out(subp8_1_out), .OverFlow(OF_ADDP8));
  // Probe on add_1_out
  Multiplexer #(.select(4), .width(16)) multiplexer_1 (
    .in0(add_1_out), .in1(sub_1_out), .in2(sllv_1_out), .in3(srlv_1_out), .in4(srav_1_out), .in5(slt_1_out),
    .in6(or_1_out), .in7(and_1_out), .in8(addp8_1_out), .in9(subp8_1_out), .out(result), .sel(switch__S));  // open: in10, in11, in12, in13, in14, in15, en
  // Probe on result
  Multiplexer #(.select(4)) multiplexer_2 (
    .in0(OF_ADD), .in1(OF_ADD), .in4(OF_ADDP8), .in5(OF_ADDP8), .in6(OF_ADDP8), .in7(OF_ADDP8),
    .in8(OF_ADDP8), .in9(OF_ADDP8), .in10(OF_ADDP8), .in11(OF_ADDP8), .in13(undriven), .in14(undriven),
    .in15(undriven), .out(signed_overflow), .sel(switch__S));  // open: in2, in3, in12, en
  Comparator #(.width(16)) comparator_1 (.a(X), .b(Y), .eq(equal));  // open: gt, lt
  // also tied to GND on the sheet: OF_ADDP8

  // Other names for the same wires on the sheet: OF_SUB = OF_ADD; OF_SUB8 = OF_ADDP8; S[3:0] = switch__S
endmodule

module AND (
  input  [15:0] X,
  input  [15:0] Y,
  output [15:0] out
);

  assign out = X & Y;  // AND_Gate and_1, 16 bits wide
endmodule

module OR (
  input  [15:0] X,
  input  [15:0] Y,
  output [15:0] out
);

  assign out = X | Y;  // OR_Gate or_1, 16 bits wide
endmodule

module ADD (
  input  [15:0] X,
  input  [15:0] Y,
  output [15:0] out,
  output OverFlow
);

  wire and_1_out, and_2_out, and_3_out, and_4_out, not_1_out, not_2_out, not_3_out, Sign_out, Sign_X, Sign_Y;

  not not_1 (not_1_out, Sign_X);
  not not_2 (not_2_out, Sign_Y);
  BitSelector #(.width(16)) bitselector_1 (.in(X), .out(Sign_X), .sel(4'b1111));
  BitSelector #(.width(16)) bitselector_2 (.in(Y), .out(Sign_Y), .sel(4'b1111));
  and and_1 (and_1_out, not_1_out, not_2_out);
  and and_2 (and_2_out, Sign_X, Sign_Y);
  and and_3 (and_3_out, and_1_out, Sign_out);
  not not_3 (not_3_out, Sign_out);
  and and_4 (and_4_out, not_3_out, and_2_out);
  Adder #(.width(16)) adder_1 (.a(X), .b(Y), .out(out));  // open: cin, cout
  or or_1 (OverFlow, and_3_out, and_4_out);
  BitSelector #(.width(16)) bitselector_3 (.in(out), .out(Sign_out), .sel(4'b1111));
endmodule

module SUB (
  input  [15:0] X,
  input  [15:0] Y,
  output [15:0] out,
  output OverFlow
);

  wire and_1_out, and_2_out, and_3_out, and_4_out, not_1_out, not_2_out, not_3_out, Sign_out, Sign_X, Sign_Y;

  not not_1 (not_1_out, Sign_X);
  not not_2 (not_2_out, Sign_Y);
  BitSelector #(.width(16)) bitselector_1 (.in(X), .out(Sign_X), .sel(4'b1111));
  BitSelector #(.width(16)) bitselector_2 (.in(Y), .out(Sign_Y), .sel(4'b1111));
  and and_1 (and_1_out, not_1_out, Sign_Y);
  and and_2 (and_2_out, Sign_X, not_2_out);
  and and_3 (and_3_out, and_1_out, Sign_out);
  not not_3 (not_3_out, Sign_out);
  and and_4 (and_4_out, not_3_out, and_2_out);
  Subtractor #(.width(16)) subtractor_1 (.a(X), .b(Y), .out(out));  // open: bin, bout
  or or_1 (OverFlow, and_3_out, and_4_out);
  BitSelector #(.width(16)) bitselector_3 (.in(out), .out(Sign_out), .sel(4'b1111));
endmodule

module SLT (
  input  [15:0] X,
  input  [15:0] Y,
  output [15:0] out
);

  wire comparator_1_lt;

  Comparator #(.width(16)) comparator_1 (.a(X), .b(Y), .lt(comparator_1_lt));  // open: gt, eq
  Multiplexer #(.width(16)) multiplexer_1 (
    .in0({16{1'b0}}), .in1(16'h1), .out(out), .sel(comparator_1_lt));  // open: en
endmodule

module SLLV (
  input  [15:0] X,
  input  [15:0] Y,
  output [15:0] out
);

  Shifter #(.width(16)) shifter_1 (.in(X), .\dist (Y[3:0]), .out(out));
endmodule

module SRLV (
  input  [15:0] X,
  input  [15:0] Y,
  output [15:0] out
);

  Shifter #(.width(16), .shift("lr")) shifter_1 (.in(X), .\dist (Y[3:0]), .out(out));
endmodule

module SRAV (
  input  [15:0] X,
  input  [15:0] Y,
  output [15:0] out
);

  Shifter #(.width(16), .shift("ar")) shifter_1 (.in(X), .\dist (Y[3:0]), .out(out));
endmodule

// AP8
module ADDP8 (
  input  [15:0] X,
  input  [15:0] Y,
  output [15:0] out,
  output OverFlow
);

  wire and_1_out, and_2_out, and_3_out, and_4_out, and_5_out, and_6_out, and_7_out, and_8_out, not_1_out,
       not_2_out, not_3_out, not_4_out, not_5_out, not_6_out, or_1_out, or_2_out, Sign_Sum_0_7,
       Sign_Sum_8_15, Sign_X_0_7, Sign_X_8_15, Sign_Y;

  not not_1 (not_1_out, Sign_X_0_7);
  not not_2 (not_2_out, Sign_Y);
  not not_3 (not_3_out, Sign_X_8_15);
  not not_4 (not_4_out, Sign_Y);
  and and_1 (and_1_out, not_1_out, not_2_out);
  and and_2 (and_2_out, Sign_X_0_7, Sign_Y);
  and and_3 (and_3_out, not_3_out, not_4_out);
  and and_4 (and_4_out, Sign_X_8_15, Sign_Y);
  BitSelector bitselector_1 (.in(X[15:8]), .out(Sign_X_8_15), .sel(3'b111));
  and and_5 (and_5_out, and_1_out, Sign_Sum_0_7);
  not not_5 (not_5_out, Sign_Sum_0_7);
  and and_6 (and_6_out, and_3_out, Sign_Sum_8_15);
  not not_6 (not_6_out, Sign_Sum_8_15);
  or or_1 (or_1_out, and_5_out, and_7_out);
  and and_7 (and_7_out, not_5_out, and_2_out);
  or or_2 (or_2_out, and_6_out, and_8_out);
  and and_8 (and_8_out, not_6_out, and_4_out);
  Adder adder_1 (.a(X[15:8]), .b(Y[15:8]), .out(out[15:8]));  // open: cin, cout
  BitSelector bitselector_2 (.in(X[7:0]), .out(Sign_X_0_7), .sel(3'b111));
  BitSelector bitselector_3 (.in(Y[7:0]), .out(Sign_Y), .sel(3'b111));
  or or_3 (OverFlow, or_1_out, or_2_out);
  Adder adder_2 (.a(X[7:0]), .b(Y[7:0]), .out(out[7:0]));  // open: cin, cout
  BitSelector bitselector_4 (.in(out[15:8]), .out(Sign_Sum_8_15), .sel(3'b111));
  BitSelector bitselector_5 (.in(out[7:0]), .out(Sign_Sum_0_7), .sel(3'b111));
endmodule

// SP8
module SUBP8 (
  input  [15:0] X,
  input  [15:0] Y,
  output [15:0] out,
  output OverFlow
);

  wire and_1_out, and_2_out, and_3_out, and_4_out, and_5_out, and_6_out, and_7_out, and_8_out, not_1_out,
       not_2_out, not_3_out, not_4_out, not_5_out, not_6_out, or_1_out, or_2_out, Sign_Sum_0_7,
       Sign_Sum_8_15, Sign_X_0_7, Sign_X_8_15, Sign_Y_0_7, Sign_Y_8_15;

  not not_1 (not_1_out, Sign_X_0_7);
  not not_2 (not_2_out, Sign_Y_0_7);
  not not_3 (not_3_out, Sign_X_8_15);
  not not_4 (not_4_out, Sign_Y_8_15);
  BitSelector bitselector_1 (.in(X[15:8]), .out(Sign_X_8_15), .sel(3'b111));
  BitSelector bitselector_2 (.in(Y[15:8]), .out(Sign_Y_8_15), .sel(3'b111));
  and and_1 (and_1_out, not_1_out, Sign_Y_0_7);
  not not_5 (not_5_out, Sign_Sum_0_7);
  and and_2 (and_2_out, Sign_X_0_7, not_2_out);
  and and_3 (and_3_out, not_3_out, Sign_Y_8_15);
  not not_6 (not_6_out, Sign_Sum_8_15);
  and and_4 (and_4_out, Sign_X_8_15, not_4_out);
  and and_5 (and_5_out, and_1_out, Sign_Sum_0_7);
  and and_6 (and_6_out, not_5_out, and_2_out);
  and and_7 (and_7_out, and_3_out, Sign_Sum_8_15);
  and and_8 (and_8_out, not_6_out, and_4_out);
  Subtractor subtractor_1 (.a(X[15:8]), .b(Y[15:8]), .out(out[15:8]));  // open: bin, bout
  or or_1 (or_1_out, and_5_out, and_6_out);
  or or_2 (or_2_out, and_7_out, and_8_out);
  BitSelector bitselector_3 (.in(X[7:0]), .out(Sign_X_0_7), .sel(3'b111));
  BitSelector bitselector_4 (.in(Y[7:0]), .out(Sign_Y_0_7), .sel(3'b111));
  or or_3 (OverFlow, or_1_out, or_2_out);
  Subtractor subtractor_2 (.a(X[7:0]), .b(Y[7:0]), .out(out[7:0]));  // open: bin, bout
  BitSelector bitselector_5 (.in(out[15:8]), .out(Sign_Sum_8_15), .sel(3'b111));
  BitSelector bitselector_6 (.in(out[7:0]), .out(Sign_Sum_0_7), .sel(3'b111));
endmodule
