// Logisim project cpu.circ as structural Verilog: 4 circuits, main circuit main
module main (
  input  [15:0] From_Instr_Mem,
  input  clk,
  output [15:0] r0,
  output [15:0] r1,
  output [15:0] r2,
  output [15:0] r3,
  output [15:0] Display_0,
  output [15:0] Display_1,
  output [15:0] To_Instr_Mem,
  output [15:0] Data_Mem_Data,
  output [15:0] Data_Mem_Addr,
  output Data_Mem_Write
);

  wire ALU_signed_overflow, ALUSrc, and_1_out, and_2_out, and_3_out, and_4_out, Branch, BranchNE,
       BranchTaken, button_1_out, comparator_2_gt, comparator_3_eq, Equal, ExtImm, flush, jal, lui, MemRead,
       MemtoReg, not_1_out, not_2_out, not_3_out, RegDst, RegWrite;
  wire [1:0] multiplexer_4_out, multiplexer_6_out, PC_sel;
  wire [3:0] ALUOp, Opcode;
  wire [5:0] funct;
  wire [11:6] Jump_To;
  wire [15:0] adder_1_out, adder_2_out, demultiplexer_1_out0, demultiplexer_1_out1, ExtendedImm, j_nextpc,
       jal_nextpc, main_1_read_data_2, multiplexer_1_out, multiplexer_2_out, multiplexer_3_out,
       multiplexer_7_out, multiplexer_8_out, multiplexer_9_out, multiplexer_10_out, newPC, rsData, WriteData;

  Adder #(.width(16)) adder_1 (.a(To_Instr_Mem), .b(16'h1), .out(adder_1_out));  // open: cin, cout
  Control Control (
    .Opcode(Opcode), .funct(funct), .RegDst(RegDst), .RegWrite(RegWrite), .ALUctr(ALUOp), .ALUsrc(ALUSrc),
    .MemWrite(Data_Mem_Write), .MemRead(MemRead), .MemtoReg(MemtoReg), .ExtImm(ExtImm), .Branch(Branch),
    .BranchNE(BranchNE), .PC_sel(PC_sel), .lui(lui));
  Multiplexer #(.width(16)) multiplexer_1 (
    .in0(From_Instr_Mem), .in1(16'h6), .out(multiplexer_1_out), .sel(flush));  // open: en
  Adder #(.width(16)) adder_2 (.a(To_Instr_Mem), .b(ExtendedImm), .out(adder_2_out));  // open: cin, cout
  Jump u_jal (.currPC(To_Instr_Mem), .TargetAddress({4'b0000, Jump_To, funct}), .nextPC(jal_nextpc));
  Jump j (.currPC(To_Instr_Mem), .TargetAddress({4'b0000, Jump_To, funct}), .nextPC(j_nextpc));
  Register #(.width(16)) register_1 (.D(multiplexer_1_out), .Q({Opcode, Jump_To, funct}), .clk(clk));  // open: en, clr
  // Probe on {Opcode, Jump_To, funct}
  // Probe on PC_sel
  Multiplexer #(.select(2), .width(16)) multiplexer_2 (
    .in0(r0), .in1(r1), .in2(r2), .in3(r3), .out(multiplexer_2_out), .sel(Jump_To[11:10]));  // open: en
  // Probe on Opcode
  Multiplexer #(.select(2), .width(16)) multiplexer_3 (
    .in0(adder_1_out), .in1(jal_nextpc), .in2(j_nextpc), .in3(multiplexer_2_out), .out(multiplexer_3_out),
    .sel(PC_sel));  // open: en
  Multiplexer #(.width(2)) multiplexer_4 (
    .in0(Jump_To[9:8]), .in1(Jump_To[7:6]), .out(multiplexer_4_out), .sel(RegDst));  // open: en
  Comparator #(.width(2), .mode("unsigned")) comparator_1 (.a(PC_sel), .b(2'b01), .eq(jal));  // open: gt, lt
  Register #(.width(16)) PC (.D(newPC), .Q(To_Instr_Mem), .clk(clk));  // open: en, clr
  // Probe on newPC
  Multiplexer #(.width(16)) multiplexer_5 (
    .in0(multiplexer_3_out), .in1(adder_2_out), .out(newPC), .sel(BranchTaken));  // open: en
  Comparator #(.width(2), .mode("unsigned")) comparator_2 (
    .a(PC_sel), .b(2'b00), .gt(comparator_2_gt));  // open: eq, lt
  Multiplexer #(.width(2)) multiplexer_6 (
    .in0(multiplexer_4_out), .in1(2'b11), .out(multiplexer_6_out), .sel(jal));  // open: en
  Multiplexer #(.width(16)) multiplexer_7 (
    .in0(WriteData), .in1(To_Instr_Mem), .out(multiplexer_7_out), .sel(jal));  // open: en
  // Probe on ALUOp
  or or_1 (flush, comparator_2_gt, BranchTaken);
  Regfile_main main_1 (
    .Read_register_1(Jump_To[11:10]), .Read_register_2(Jump_To[9:8]), .write_register(multiplexer_6_out),
    .write_data(multiplexer_7_out), .Reg_0_Value(r0), .Reg_1_Value(r1), .Reg_2_Value(r2), .Reg_3_Value(r3),
    .RegWrite(RegWrite), .clock(clk), .Read_Data_1(rsData), .Read_Data_2(main_1_read_data_2));
  SignExt u_ExtImm (.in_1({Jump_To[7:6], funct}), .Ext(ExtImm), .out_3(ExtendedImm));
  Multiplexer #(.width(16)) multiplexer_8 (
    .in0(rsData), .in1(ExtendedImm), .out(multiplexer_8_out), .sel(lui));  // open: en
  Comparator #(.width(4), .mode("unsigned")) comparator_3 (
    .a(Opcode), .b(4'b1100), .eq(comparator_3_eq));  // open: gt, lt
  and and_1 (and_1_out, Branch, Equal);
  not not_1 (not_1_out, Equal);
  and and_2 (and_2_out, not_1_out, BranchNE);
  Hex_Digit_Display hex_digit_display_1 (.value(Display_0[15:12]));  // open: dp
  Hex_Digit_Display hex_digit_display_2 (.value(Display_0[11:8]));  // open: dp
  Multiplexer #(.width(16)) multiplexer_9 (
    .in0(main_1_read_data_2), .in1(ExtendedImm), .out(multiplexer_9_out), .sel(ALUSrc));  // open: en
  Demultiplexer #(.width(16), .enable("false")) demultiplexer_1 (
    .out0(demultiplexer_1_out0), .out1(demultiplexer_1_out1), .in(rsData), .sel(ExtendedImm[0]));
  not not_2 (not_2_out, ExtendedImm[0]);
  or or_2 (BranchTaken, and_1_out, and_2_out);
  Hex_Digit_Display hex_digit_display_3 (.value(Display_0[7:4]));  // open: dp
  Hex_Digit_Display hex_digit_display_4 (.value(Display_0[3:0]));  // open: dp
  alu_main ALU (
    .switch__S(ALUOp), .X(multiplexer_8_out), .equal(Equal), .result(Data_Mem_Addr),
    .signed_overflow(ALU_signed_overflow), .Y(multiplexer_10_out));
  Multiplexer #(.width(16)) multiplexer_10 (
    .in0(multiplexer_9_out), .in1(16'h8), .out(multiplexer_10_out), .sel(lui));  // open: en
  Register #(.width(16)) register_2 (.D(demultiplexer_1_out0), .en(and_3_out), .Q(Display_0), .clk(clk));  // open: clr
  and and_3 (and_3_out, not_2_out, comparator_3_eq);
  Register #(.width(16)) register_3 (.D(demultiplexer_1_out1), .en(and_4_out), .Q(Display_1), .clk(clk));  // open: clr
  and and_4 (and_4_out, comparator_3_eq, ExtendedImm[0]);
  Hex_Digit_Display hex_digit_display_5 (.value(Display_1[15:12]));  // open: dp
  LED Overflow (.in(ALU_signed_overflow));
  Hex_Digit_Display hex_digit_display_6 (.value(Display_1[11:8]));  // open: dp
  Hex_Digit_Display hex_digit_display_7 (.value(Display_1[7:4]));  // open: dp
  Button button_1 (.out(button_1_out));
  not not_3 (not_3_out, Data_Mem_Write);
  Multiplexer #(.width(16)) multiplexer_11 (
    .in0(Data_Mem_Addr), .in1(Data_Mem_Data), .out(WriteData), .sel(MemtoReg));  // open: en
  Hex_Digit_Display hex_digit_display_8 (.value(Display_1[3:0]));  // open: dp
  assign Data_Mem_Data = Data_Mem_Write ? main_1_read_data_2 : 16'bz;  // Controlled_Buffer controlled_buffer_1
  RAM #(.addrWidth(16), .dataWidth(16)) ram_1 (
    .addr(Data_Mem_Addr), .data(Data_Mem_Data), .sel(1'b1), .clk(clk), .ld(not_3_out), .clr(button_1_out));

  // Other names for the same wires on the sheet: Jump_To[5:0] = funct; rs[1:0] = Jump_To[11:10];
  //   currPC[15:0] = To_Instr_Mem; d0[15:0] = Display_0; d1[15:0] = Display_1; MemWrite = Data_Mem_Write

  // Notes on the sheet:
  //   jr
  //   PC_sel: 00 = currPC+1, 01 =  jal, 10 = j, 11 = jr
endmodule

module SignExt (
  input  [7:0] in_1,
  input  Ext,
  output [15:0] out_3
);

  wire bitselector_1_out, multiplexer_2_out;

  BitSelector bitselector_1 (.in(in_1), .out(bitselector_1_out), .sel(3'b111));
  Multiplexer #(.width(8)) multiplexer_1 (
    .in0({8{1'b0}}), .in1({8{1'b1}}), .out(out_3[15:8]), .sel(multiplexer_2_out));  // open: en
  Multiplexer multiplexer_2 (.in0(1'b0), .in1(bitselector_1_out), .out(multiplexer_2_out), .sel(Ext));  // open: en

  assign out_3[7:0] = in_1;
endmodule

module Control (
  input  [3:0] Opcode,
  input  [5:0] funct,
  output RegDst,
  output RegWrite,
  output [3:0] ALUctr,
  output ALUsrc,
  output MemWrite,
  output MemRead,
  output MemtoReg,
  output ExtImm,
  output Branch,
  output BranchNE,
  output [1:0] PC_sel,
  output lui
);

  wire add, addi, addp8, \and , andi, disp, j, jal, jr, not_1_out, not_2_out, not_3_out, not_4_out,
       not_5_out, not_6_out, not_7_out, not_8_out, \or , ori, sllv, slt, srav, srlv, sub, subp8, undefined;
  wire [3:0] B0_2_out;

  not not_1 (not_1_out, funct[3]);
  not not_2 (not_2_out, funct[2]);
  not not_3 (not_3_out, Opcode[3]);
  not not_4 (not_4_out, Opcode[2]);
  not not_5 (not_5_out, funct[1]);
  not not_6 (not_6_out, Opcode[1]);
  not not_7 (not_7_out, funct[0]);
  not not_8 (not_8_out, Opcode[0]);
  and u_add (add, not_1_out, not_2_out, not_5_out, not_7_out, RegDst);
  and u_sub (sub, not_1_out, not_2_out, not_5_out, funct[0], RegDst);
  and u_sllv (sllv, not_1_out, not_2_out, funct[1], not_7_out, RegDst);
  and u_srlv (srlv, not_1_out, not_2_out, funct[1], funct[0], RegDst);
  and u_srav (srav, not_1_out, funct[2], not_5_out, not_7_out, RegDst);
  and u_slt (slt, not_1_out, funct[2], not_5_out, funct[0], RegDst);
  and u_or (\or , not_1_out, funct[2], funct[1], not_7_out, RegDst);
  and u_and (\and , not_1_out, funct[2], funct[1], funct[1], RegDst);
  and u_addp8 (addp8, funct[3], not_2_out, not_5_out, not_7_out, RegDst);
  and u_subp8 (subp8, funct[3], not_2_out, not_5_out, funct[0], RegDst);
  and R_Type (RegDst, not_3_out, not_4_out, not_6_out, not_8_out);
  and u_jal (jal, not_3_out, not_4_out, not_6_out, Opcode[0]);
  and u_j (j, not_3_out, not_4_out, Opcode[1], not_8_out);
  and u_jr (jr, not_3_out, not_4_out, Opcode[1], Opcode[0]);
  and beq (Branch, not_3_out, Opcode[2], not_6_out, not_8_out);
  and u_addi (addi, not_3_out, Opcode[2], not_6_out, Opcode[0]);
  and u_andi (andi, not_3_out, Opcode[2], Opcode[1], not_8_out);
  and u_ori (ori, not_3_out, Opcode[2], Opcode[1], Opcode[0]);
  and bne (BranchNE, Opcode[3], not_4_out, not_6_out, not_8_out);
  and sw (MemWrite, Opcode[3], not_4_out, not_6_out, Opcode[0]);
  and u_lui (lui, Opcode[3], not_4_out, Opcode[1], not_8_out);
  and lw (MemtoReg, Opcode[3], not_4_out, Opcode[1], Opcode[0]);
  and u_disp (disp, Opcode[3], Opcode[2], not_6_out, not_8_out);
  Comparator #(.width(6)) comparator_1 (.a(funct), .b(6'b001001), .gt(undefined));  // open: eq, lt
  not not_9 (MemRead, MemWrite);
  or B2 (B0_2_out[2], ori, andi);
  buf B3 (B0_2_out[3], 1'b0);  // OR_Gate
  or or_2 (RegWrite, lui, RegDst, andi, ori, addi, MemtoReg, jal);
  or or_3 (ExtImm, addi, Branch, BranchNE, MemtoReg, MemWrite);
  or B0 (PC_sel[0], jal, jr);
  buf B0_2 (B0_2_out[0], andi);  // OR_Gate
  or B1 (B0_2_out[1], lui, ori, andi);
  or B1_2 (PC_sel[1], j, jr);
  // Probe on PC_sel
  Multiplexer #(.width(4)) multiplexer_1 (.in0(B0_2_out), .in1(funct[3:0]), .out(ALUctr), .sel(RegDst));  // open: en
  // Probe on ALUctr
  or or_4 (ALUsrc, andi, ori, addi, lui, MemtoReg, MemWrite, disp);

  // Other names for the same wires on the sheet: beq = Branch; bne = BranchNE; lw = MemtoReg; R_Type = RegDst;
  //   sw = MemWrite

  // Notes on the sheet:
  //   00 = currPC+1, 01 =  jal, 10 = j, 11 = jr
endmodule

module Jump (
  input  [15:0] currPC,
  input  [15:0] TargetAddress,
  output [15:0] nextPC
);

  wire [15:0] and_1_out;

  assign and_1_out = currPC & 16'hf000;  // AND_Gate and_1, 16 bits wide
  assign nextPC = and_1_out | TargetAddress;  // OR_Gate or_1, 16 bits wide
endmodule
